# Fritzing sketch Schematic (saved by Fritzing 0.9.4)
breadboards: 1

parts:
  Raspberry_Pi_1 = Raspberry Pi 3 [part_number=RPI-3-V1.2]
  Part1 = Arduino Uno (Rev3)
  Part2 = Adafruit DRV8833 DC/Stepper Motor Driver [part_number="Adafruit #3297"]
  J1 = Basic Servo
  Part3 = Adafruit VL530X Time of Flight Distance Sensor [part_number="Adafruit #3317"]
  M1 = DC Motor
  M2 = DC Motor
  VCC1 = Battery block 9V

nets:
  GND: Raspberry_Pi_1.GND, Part1.GND, Part2.GND, J1.gnd, Part3.GND, Part3.XSHUT, VCC1.-
  N1: Part1.A4/SDA, Part3.SDA
  N2: Part1.A5/SCL, Part3.SCL
  N3: Part1.D9_PWM, Part2.BIN1
  N4: Part1.D10_PWM/SS, Part2.BIN2
  N5: Part1.D2, Part3.GPIO
  N6: Part1.D3_PWM, J1.pulse
  N7: Part1.D4, Part2.NFAULT
  N8: Part1.D5_PWM, Part2.AIN1
  N9: Part1.D6_PWM, Part2.AIN2
  5V: Part1.5V, J1.vcc, Part3.VCC
  N10: Part2.AOUT2, M2.pin_1
  N11: Part2.AOUT1, M2.pin_2
  N12: Part2.BOUT1, M1.pin_1
  N13: Part2.BOUT2, M1.pin_2
  9VIN: Part2.VMOTOR, VCC1.+

notes:
  ??
  RoboCar, Schematic of RoboCar. Group 3., 1

custom parts:
  Adafruit DRV8833 DC/Stepper Motor Driver: Spin two DC motors or step one bi-polar or uni-polar stepper with up to 1.2A per channel using the DRV8833. This motor driver chip is a nice alternative to the TB6612 driver. Like that chip, you get 2 full H-bridges, but this chip is better for low voltage uses (can run from 2.7V up to 10.8V motor power) and has built in current limiting capability. We set it up for 1A current limiting so you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
  Adafruit VL530X Time of Flight Distance Sensor: The VL53L0X is a Time of Flight distance sensor like no other you've used! The sensor contains a very tiny invisible laser source, and a matching sensor. The VL53L0X can detect the "time of flight", or how long the light has taken to bounce back to the sensor. Since it uses a very narrow light source, it is good for determining distance of only the surface directly in front of it. Unlike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
